// Logisim project cpu.circ as structural Verilog: 3 circuits, main circuit main
module main (
  input  in_1
);

  wire alu_force_cin, alu_inv_a, alu_inv_b, alu_inv_out, alu_sel_0, alu_sel_1, alu_sel_2, and_1_out,
       and_2_out, and_3_out, and_4_out, blank_alu_b, CARRY_OUT, CARRY_q, CARRY_qn, CK, comparator_1_eq,
       COND_FLAG, cond_inv, cond_sel_0, cond_sel_1, dec_sp, decoder_1_out0, decoder_1_out1, decoder_1_out2,
       decoder_1_out3, decoder_2_out0, decoder_2_out1, decoder_2_out2, decoder_2_out3, decoder_2_out4,
       decoder_2_out5, decoder_2_out6, decoder_2_out7, GREATER_THAN_ZERO, GREATER_THAN_ZERO_q,
       GREATER_THAN_ZERO_qn, imm_8_b, imm_8_se, inc_sp, jmp, jmp_cond, jmp_jtr, jmp_rel, LESS_THAN_ZERO,
       LESS_THAN_ZERO_q, LESS_THAN_ZERO_qn, mem_read, mem_read_se, mem_width_8, mem_width_16, mem_width_32,
       mem_write, MISALIGNED_ACCESS, next_instruction, next_uop, not_1_out, not_2_out, not_3_out, not_4_out,
       not_5_out, not_6_out, not_9_out, or_1_out, or_2_out, or_3_out, read_a, read_b, reg_override_a,
       reg_override_b, reg_override_w, reg_r_addr_0, reg_r_addr_1, reg_r_addr_2, reg_r_addr_3, reg_w_addr_0,
       reg_w_addr_1, reg_w_addr_2, reg_w_addr_3, RS, se_imm, set_flags, set_jtr, w_high, w_low, w_sel_imm,
       w_sel_mem, w_sel_pc, ZERO, ZERO_q, ZERO_qn;
  wire [3:0] A_ADDR, B_ADDR, bit_extender_1_out, bit_extender_2_out, bit_extender_3_out, counter_1_q,
       multiplexer_6_out, W_ADDR;
  wire [4:0] bit_extender_16_out;
  wire [7:0] bit_extender_4_out, IMM_8, IMM_24, INSTR_OP, multiplexer_7_out, multiplexer_8_out,
       multiplexer_9_out, multiplexer_10_out, multiplexer_23_out;
  wire [15:0] bit_extender_5_out, bit_extender_7_out, bit_extender_11_out, multiplexer_11_out,
       multiplexer_12_out, multiplexer_24_out;
  wire [15:8] IMM_16;
  wire [20:5] multiplexer_2_out;
  wire [31:0] A_DATA, adder_1_out, adder_3_out, and_5_out, B_DATA, bit_extender_6_out, bit_extender_8_out,
       bit_extender_9_out, bit_extender_10_out, bit_extender_12_out, bit_extender_13_out,
       bit_extender_14_out, bit_extender_15_out, controlled_buffer_1_out, controlled_buffer_7_out, FROM_MEM,
       MEM_ADDR, multiplexer_14_out, multiplexer_15_out, multiplexer_16_out, multiplexer_18_out,
       multiplexer_20_out, multiplexer_21_out, multiplexer_22_out, multiplexer_25_out, multiplexer_26_out,
       multiplexer_27_out, not_7_out, not_8_out, not_10_out, PC_CURRENT, PC_PLUS_1, pull_resistor_2_node,
       ram_1_data, regfile_1_out_13, regfile_1_out_14, regfile_1_out_15, regfile_1_out_16, regfile_1_out_17,
       regfile_1_out_18, regfile_1_out_19, regfile_1_out_20, regfile_1_out_21, regfile_1_out_22,
       regfile_1_out_23, regfile_1_out_24, regfile_1_out_25, regfile_1_out_26, regfile_1_out_27,
       regfile_1_out_28, register_1_q, rom_1_data, rom_2_data, shifter_1_out, shifter_2_out, shifter_3_out,
       shifter_4_out, shifter_5_out, TO_MEM, W_DATA, xor_1_out;

  not not_1 (not_1_out, next_uop);
  Pull_Resistor pull_resistor_1 (.node(next_uop));
  Counter #(.width(4), .max('hf)) counter_1 (
    .load(not_1_out), .count(next_uop), .Q(counter_1_q), .clk(CK), .clr(RS));  // open: D, carry
  ROM #(.addrWidth(12), .dataWidth(32)) rom_1 (.addr({INSTR_OP, counter_1_q}), .data(rom_1_data));  // open: sel
  ROM #(.addrWidth(12), .dataWidth(32)) rom_2 (.addr({INSTR_OP, counter_1_q}), .data(rom_2_data));  // open: sel
  Multiplexer #(.width(32), .disabled(0), .enable("false")) multiplexer_1 (
    .in0(32'h40005), .in1(rom_1_data),
    .out({mem_read_se, mem_width_8, mem_width_16, mem_width_32, mem_write, mem_read, imm_8_se, jmp_cond, cond_inv, cond_sel_1, cond_sel_0, set_flags, imm_8_b, jmp_jtr, alu_force_cin, alu_sel_2, alu_sel_1, alu_sel_0, alu_inv_out, alu_inv_b, alu_inv_a, w_sel_mem, se_imm, w_sel_imm, read_b, read_a, w_low, w_high, jmp_rel, jmp, next_uop, next_instruction}),
    .sel(1'b1));
  Multiplexer #(.width(32), .disabled(0), .enable("false")) multiplexer_2 (
    .in0({32{1'b0}}), .in1(rom_2_data),
    .out({reg_w_addr_3, reg_w_addr_2, reg_w_addr_1, reg_w_addr_0, reg_override_w, reg_r_addr_3, reg_r_addr_2, reg_r_addr_1, reg_r_addr_0, reg_override_b, reg_override_a, multiplexer_2_out, set_jtr, blank_alu_b, w_sel_pc, dec_sp, inc_sp}),
    .sel(1'b1));
  D_Flip_Flop u_ZERO (.clk(CK), .D(ZERO), .Q(ZERO_q), .Qn(ZERO_qn), .en(set_flags), .reset(RS));  // open: preset
  D_Flip_Flop CARRY (.clk(CK), .D(CARRY_OUT), .Q(CARRY_q), .Qn(CARRY_qn), .en(set_flags), .reset(RS));  // open: preset
  D_Flip_Flop u_LESS_THAN_ZERO (
    .clk(CK), .D(LESS_THAN_ZERO), .Q(LESS_THAN_ZERO_q), .Qn(LESS_THAN_ZERO_qn), .en(set_flags), .reset(RS));  // open: preset
  D_Flip_Flop u_GREATER_THAN_ZERO (
    .clk(CK), .D(GREATER_THAN_ZERO), .Q(GREATER_THAN_ZERO_q), .Qn(GREATER_THAN_ZERO_qn), .en(set_flags),
    .reset(RS));  // open: preset
  Multiplexer #(.select(3), .disabled(0), .enable("false")) multiplexer_3 (
    .in0(ZERO_q), .in1(ZERO_qn), .in2(CARRY_q), .in3(CARRY_qn), .in4(LESS_THAN_ZERO_q),
    .in5(LESS_THAN_ZERO_qn), .in6(GREATER_THAN_ZERO_q), .in7(GREATER_THAN_ZERO_qn), .out(COND_FLAG),
    .sel({cond_sel_0, cond_sel_1, cond_inv}));
  // Probe on 32'h40005
  // Probe on {32{1'b0}}
  // Probe on PC_CURRENT
  // Probe on INSTR_OP
  // Probe on IMM_16
  // Probe on IMM_8
  // Probe on IMM_24
  // Probe on {IMM_16, IMM_8, IMM_24}
  // Probe on {IMM_16, IMM_8}
  // Probe on IMM_8
  // Probe on A_DATA
  // Probe on B_DATA
  // Probe on W_DATA
  // Probe on A_ADDR
  // Probe on B_ADDR
  // Probe on W_ADDR
  // Probe on MEM_ADDR
  // Probe on TO_MEM
  // Probe on FROM_MEM
  Bit_Extender #(.out_width(4)) bit_extender_1 (.in(IMM_24), .out(bit_extender_1_out));
  Bit_Extender #(.out_width(4)) bit_extender_2 (.in(IMM_16), .out(bit_extender_2_out));
  Bit_Extender #(.out_width(4)) bit_extender_3 (.in(IMM_8), .out(bit_extender_3_out));
  Bit_Extender #(.in_width(32), .out_width(8)) bit_extender_4 (.in(TO_MEM), .out(bit_extender_4_out));
  Bit_Extender #(.in_width(32)) bit_extender_5 (.in(TO_MEM), .out(bit_extender_5_out));
  Multiplexer #(.width(4), .disabled(0), .enable("false")) multiplexer_4 (
    .in0(bit_extender_1_out), .in1({reg_w_addr_3, reg_w_addr_2, reg_w_addr_1, reg_w_addr_0}), .out(W_ADDR),
    .sel(reg_override_w));
  Multiplexer #(.width(4), .disabled(0), .enable("false")) multiplexer_5 (
    .in0(bit_extender_2_out), .in1({reg_r_addr_3, reg_r_addr_2, reg_r_addr_1, reg_r_addr_0}), .out(A_ADDR),
    .sel(reg_override_a));
  Multiplexer #(.width(4), .disabled(0), .enable("false")) multiplexer_6 (
    .in0(bit_extender_3_out), .in1({reg_r_addr_3, reg_r_addr_2, reg_r_addr_1, reg_r_addr_0}),
    .out(multiplexer_6_out), .sel(reg_override_b));
  Multiplexer #(.width(8), .disabled(0), .enable("false")) multiplexer_7 (
    .in0(ram_1_data[7:0]), .in1(bit_extender_4_out), .out(multiplexer_7_out), .sel(decoder_1_out0));
  Multiplexer #(.width(8), .disabled(0), .enable("false")) multiplexer_8 (
    .in0(ram_1_data[15:8]), .in1(bit_extender_4_out), .out(multiplexer_8_out), .sel(decoder_1_out1));
  Multiplexer #(.width(8), .disabled(0), .enable("false")) multiplexer_9 (
    .in0(ram_1_data[23:16]), .in1(bit_extender_4_out), .out(multiplexer_9_out), .sel(decoder_1_out2));
  Multiplexer #(.width(8), .disabled(0), .enable("false")) multiplexer_10 (
    .in0(ram_1_data[31:24]), .in1(bit_extender_4_out), .out(multiplexer_10_out), .sel(decoder_1_out3));
  Multiplexer #(.width(16), .disabled(0), .enable("false")) multiplexer_11 (
    .in0(bit_extender_5_out), .in1(ram_1_data[15:0]), .out(multiplexer_11_out), .sel(not_2_out));
  not not_2 (not_2_out, MEM_ADDR[0]);
  Multiplexer #(.width(16), .disabled(0), .enable("false")) multiplexer_12 (
    .in0(bit_extender_5_out), .in1(ram_1_data[31:16]), .out(multiplexer_12_out), .sel(MEM_ADDR[0]));
  Multiplexer #(.width(4), .disabled(0), .enable("false")) multiplexer_13 (
    .in0(W_ADDR), .in1(multiplexer_6_out), .out(B_ADDR), .sel(not_3_out));
  not not_3 (not_3_out, mem_write);
  or or_1 (or_1_out, COND_FLAG, ~jmp_cond);  // OR_Gate
  assign bit_extender_6_out = {{8{IMM_16[15]}}, {IMM_16, IMM_8, IMM_24}};  // Bit_Extender bit_extender_6
  Register #(.width(32)) register_1 (.D(B_DATA), .en(set_jtr), .Q(register_1_q), .clk(CK), .clr(RS));
  Decoder #(.select(2), .disabled(0), .enable("false")) decoder_1 (
    .out0(decoder_1_out0), .out1(decoder_1_out1), .out2(decoder_1_out2), .out3(decoder_1_out3),
    .sel(MEM_ADDR[1:0]));
  and and_1 (and_1_out, or_1_out, jmp);
  Multiplexer #(.width(32), .enable("false")) multiplexer_14 (
    .in0(bit_extender_6_out), .in1(register_1_q), .out(multiplexer_14_out), .sel(jmp_jtr));
  // Probe on multiplexer_14_out
  assign controlled_buffer_1_out = mem_width_8 ? {multiplexer_10_out, multiplexer_9_out, multiplexer_8_out, multiplexer_7_out} : 32'bz;  // Controlled_Buffer controlled_buffer_1
  assign controlled_buffer_1_out = mem_width_16 ? {multiplexer_12_out, multiplexer_11_out} : 32'bz;  // Controlled_Buffer controlled_buffer_2
  Adder #(.width(32)) adder_1 (.a(multiplexer_15_out), .b(multiplexer_14_out), .out(adder_1_out));  // open: cin, cout
  assign controlled_buffer_1_out = mem_width_32 ? TO_MEM : 32'bz;  // Controlled_Buffer controlled_buffer_3
  // Probe on regfile_1_out_15
  // Probe on regfile_1_out_16
  // Probe on regfile_1_out_17
  // Probe on regfile_1_out_18
  // Probe on regfile_1_out_19
  // Probe on regfile_1_out_20
  // Probe on regfile_1_out_21
  // Probe on regfile_1_out_22
  // Probe on regfile_1_out_23
  // Probe on regfile_1_out_24
  // Probe on regfile_1_out_25
  // Probe on regfile_1_out_26
  // Probe on regfile_1_out_27
  // Probe on regfile_1_out_28
  // Probe on regfile_1_out_13
  // Probe on regfile_1_out_14
  Multiplexer #(.width(32), .enable("false")) multiplexer_15 (
    .in0({32{1'b0}}), .in1(PC_CURRENT), .out(multiplexer_15_out), .sel(jmp_rel));
  Counter #(.width(32), .max('hffffffff)) counter_2 (
    .load(and_1_out), .D(adder_1_out), .count(and_2_out), .Q(PC_CURRENT), .clk(CK), .clr(RS));  // open: carry
  and and_2 (and_2_out, ~and_1_out, next_instruction);  // AND_Gate
  Bit_Extender #(.in_width(30)) bit_extender_7 (.in(MEM_ADDR[31:2]), .out(bit_extender_7_out));
  regfile regfile_1 (
    .in_4(w_high), .in_5(w_low), .in_6(W_ADDR), .in_7(read_a), .in_8(A_ADDR), .in_9(read_b), .in_10(B_ADDR),
    .out_29(A_DATA), .out_30(TO_MEM), .in_11(CK), .in_12(RS), .in_1(W_DATA), .out_15(regfile_1_out_15),
    .out_16(regfile_1_out_16), .out_17(regfile_1_out_17), .out_18(regfile_1_out_18),
    .out_19(regfile_1_out_19), .out_20(regfile_1_out_20), .out_21(regfile_1_out_21),
    .out_22(regfile_1_out_22), .out_23(regfile_1_out_23), .out_24(regfile_1_out_24),
    .out_25(regfile_1_out_25), .out_26(regfile_1_out_26), .out_27(regfile_1_out_27),
    .out_28(regfile_1_out_28), .out_13(regfile_1_out_13), .out_14(regfile_1_out_14), .in_2(dec_sp),
    .in_3(inc_sp));
  Pull_Resistor pull_resistor_2 (.node(pull_resistor_2_node));
  or or_2 (or_2_out, mem_write, or_3_out);
  Multiplexer #(.width(32), .enable("false")) multiplexer_16 (
    .in0({IMM_16, IMM_8, IMM_16, IMM_8}), .in1(bit_extender_8_out), .out(multiplexer_16_out), .sel(se_imm));
  assign bit_extender_8_out = {{16{IMM_16[15]}}, {IMM_16, IMM_8}};  // Bit_Extender bit_extender_8
  not not_4 (not_4_out, w_sel_imm);
  Multiplexer #(.width(32), .enable("false")) multiplexer_17 (
    .in0(multiplexer_16_out), .in1(multiplexer_18_out), .out(W_DATA), .sel(not_4_out));
  assign bit_extender_9_out = {{24{1'b0}}, IMM_8};  // Bit_Extender bit_extender_9
  assign bit_extender_10_out = {{24{IMM_8[7]}}, IMM_8};  // Bit_Extender bit_extender_10
  Clock clock_1 (.out(CK));
  Button button_1 (.out(RS));
  Bit_Extender #(.in_width(32)) bit_extender_11 (.in(PC_CURRENT), .out(bit_extender_11_out));
  Adder #(.width(32)) adder_2 (.a(PC_CURRENT), .b(pull_resistor_2_node), .out(PC_PLUS_1), .cin(1'b1));  // open: cout
  // Probe on PC_PLUS_1
  RAM #(.addrWidth(16), .dataWidth(32), .bus("separate")) ram_1 (
    .addr(bit_extender_7_out), .din(controlled_buffer_1_out), .data(ram_1_data), .str(mem_write),
    .sel(or_2_out), .clk(CK), .ld(or_3_out), .clr(RS));
  or or_3 (or_3_out, mem_write, mem_read);
  not not_5 (not_5_out, w_sel_mem);
  Multiplexer #(.width(32), .enable("false")) multiplexer_18 (
    .in0(FROM_MEM), .in1(multiplexer_21_out), .out(multiplexer_18_out), .sel(not_5_out));
  Multiplexer #(.width(32), .disabled(0)) multiplexer_19 (
    .in0(TO_MEM), .in1(multiplexer_20_out), .out(B_DATA), .sel(imm_8_b), .en(not_9_out));
  Multiplexer #(.width(32), .disabled(0), .enable("false")) multiplexer_20 (
    .in0(bit_extender_9_out), .in1(bit_extender_10_out), .out(multiplexer_20_out), .sel(imm_8_se));
  Comparator #(.width(2)) comparator_1 (.a(2'b00), .b(MEM_ADDR[1:0]), .eq(comparator_1_eq));  // open: gt, lt
  not not_6 (not_6_out, w_sel_pc);
  Multiplexer #(.width(32), .enable("false")) multiplexer_21 (
    .in0(PC_PLUS_1), .in1(MEM_ADDR), .out(multiplexer_21_out), .sel(not_6_out));
  Multiplexer #(.width(32), .disabled(0), .enable("false")) multiplexer_22 (
    .in0(A_DATA), .in1(not_7_out), .out(multiplexer_22_out), .sel(alu_inv_a));
  assign not_7_out = ~A_DATA;  // NOT_Gate not_7, 32 bits wide
  assign not_8_out = ~B_DATA;  // NOT_Gate not_8, 32 bits wide
  not not_9 (not_9_out, blank_alu_b);
  ROM #(.addrWidth(16), .dataWidth(32)) rom_3 (
    .addr(bit_extender_11_out), .data({INSTR_OP, IMM_16, IMM_8, IMM_24}), .sel(1'b1));
  and and_3 (and_3_out, mem_width_32, ~comparator_1_eq);  // AND_Gate
  and and_4 (and_4_out, mem_width_16, MEM_ADDR[0]);
  Multiplexer #(.select(2), .width(8), .disabled(0), .enable("false")) multiplexer_23 (
    .in0(ram_1_data[7:0]), .in1(ram_1_data[15:8]), .in2(ram_1_data[23:16]), .in3(ram_1_data[31:24]),
    .out(multiplexer_23_out), .sel(MEM_ADDR[1:0]));
  Multiplexer #(.width(16), .disabled(0), .enable("false")) multiplexer_24 (
    .in0(ram_1_data[15:0]), .in1(ram_1_data[31:16]), .out(multiplexer_24_out), .sel(MEM_ADDR[1]));
  Multiplexer #(.width(32), .disabled(0), .enable("false")) multiplexer_25 (
    .in0(B_DATA), .in1(not_8_out), .out(multiplexer_25_out), .sel(alu_inv_b));
  or or_4 (MISALIGNED_ACCESS, and_3_out, and_4_out);
  assign bit_extender_12_out = {{24{1'b0}}, multiplexer_23_out};  // Bit_Extender bit_extender_12
  Multiplexer #(.width(32), .disabled(0), .enable("false")) multiplexer_26 (
    .in0(bit_extender_12_out), .in1(bit_extender_13_out), .out(multiplexer_26_out), .sel(mem_read_se));
  assign bit_extender_13_out = {{24{multiplexer_23_out[7]}}, multiplexer_23_out};  // Bit_Extender bit_extender_13
  assign bit_extender_14_out = {{16{1'b0}}, multiplexer_24_out};  // Bit_Extender bit_extender_14
  Multiplexer #(.width(32), .disabled(0), .enable("false")) multiplexer_27 (
    .in0(bit_extender_14_out), .in1(bit_extender_15_out), .out(multiplexer_27_out), .sel(mem_read_se));
  assign bit_extender_15_out = {{16{multiplexer_24_out[15]}}, multiplexer_24_out};  // Bit_Extender bit_extender_15
  Adder #(.width(32)) adder_3 (
    .a(multiplexer_22_out), .b(multiplexer_25_out), .out(adder_3_out), .cin(alu_force_cin), .cout(CARRY_OUT));
  assign and_5_out = multiplexer_25_out & multiplexer_22_out;  // AND_Gate and_5, 32 bits wide
  assign xor_1_out = multiplexer_22_out ^ multiplexer_25_out;  // XOR_Gate xor_1, 32 bits wide
  Bit_Extender #(.in_width(32), .out_width(5)) bit_extender_16 (.in(multiplexer_25_out), .out(bit_extender_16_out));
  assign FROM_MEM = mem_width_8 ? multiplexer_26_out : 32'bz;  // Controlled_Buffer controlled_buffer_4
  assign FROM_MEM = mem_width_16 ? multiplexer_27_out : 32'bz;  // Controlled_Buffer controlled_buffer_5
  assign FROM_MEM = mem_width_32 ? ram_1_data : 32'bz;  // Controlled_Buffer controlled_buffer_6
  Decoder #(.select(3), .disabled(0), .enable("false")) decoder_2 (
    .out0(decoder_2_out0), .out1(decoder_2_out1), .out2(decoder_2_out2), .out3(decoder_2_out3),
    .out4(decoder_2_out4), .out5(decoder_2_out5), .out6(decoder_2_out6), .out7(decoder_2_out7),
    .sel({alu_sel_2, alu_sel_1, alu_sel_0}));
  assign controlled_buffer_7_out = decoder_2_out0 ? adder_3_out : 32'bz;  // Controlled_Buffer controlled_buffer_7
  assign controlled_buffer_7_out = decoder_2_out1 ? and_5_out : 32'bz;  // Controlled_Buffer controlled_buffer_8
  assign controlled_buffer_7_out = decoder_2_out2 ? xor_1_out : 32'bz;  // Controlled_Buffer controlled_buffer_9
  Shifter #(.width(32)) shifter_1 (.in(multiplexer_22_out), .\dist (bit_extender_16_out), .out(shifter_1_out));
  Shifter #(.width(32), .shift("lr")) shifter_2 (
    .in(multiplexer_22_out), .\dist (bit_extender_16_out), .out(shifter_2_out));
  Shifter #(.width(32), .shift("ar")) shifter_3 (
    .in(multiplexer_22_out), .\dist (bit_extender_16_out), .out(shifter_3_out));
  Shifter #(.width(32), .shift("rl")) shifter_4 (
    .in(multiplexer_22_out), .\dist (bit_extender_16_out), .out(shifter_4_out));
  Shifter #(.width(32), .shift("rr")) shifter_5 (
    .in(multiplexer_22_out), .\dist (bit_extender_16_out), .out(shifter_5_out));
  Pull_Resistor pull_resistor_3 (.node(FROM_MEM));
  assign controlled_buffer_7_out = decoder_2_out3 ? shifter_1_out : 32'bz;  // Controlled_Buffer controlled_buffer_10
  assign controlled_buffer_7_out = decoder_2_out4 ? shifter_2_out : 32'bz;  // Controlled_Buffer controlled_buffer_11
  assign controlled_buffer_7_out = decoder_2_out5 ? shifter_3_out : 32'bz;  // Controlled_Buffer controlled_buffer_12
  assign controlled_buffer_7_out = decoder_2_out6 ? shifter_4_out : 32'bz;  // Controlled_Buffer controlled_buffer_13
  assign controlled_buffer_7_out = decoder_2_out7 ? shifter_5_out : 32'bz;  // Controlled_Buffer controlled_buffer_14
  Multiplexer #(.width(32), .disabled(0), .enable("false")) multiplexer_28 (
    .in0(controlled_buffer_7_out), .in1(not_10_out), .out(MEM_ADDR), .sel(alu_inv_out));
  assign not_10_out = ~controlled_buffer_7_out;  // NOT_Gate not_10, 32 bits wide
  Comparator #(.width(32)) comparator_2 (
    .a(MEM_ADDR), .b({32{1'b0}}), .gt(GREATER_THAN_ZERO), .eq(ZERO), .lt(LESS_THAN_ZERO));

  // Other names for the same wires on the sheet: IMM_16[7:0] = IMM_8; IMM_24[23:8] = {IMM_16, IMM_8};
  //   INSTR_B[7:0] = IMM_8; INSTR_A[7:0] = IMM_16; INSTR_C[7:0] = IMM_24

  // Notes on the sheet:
  //   Micro op ROM
  //   contents of rom_1 (hex, n*v repeats v):
  //   16*0 331 15*0 121 15*0 111 15*0 7871 15*0 f1 15*0 80071 31*0 210f1 15*0 a1071 175*0 1210c1 15*0 d
  //   15*0 100000d 15*0 180000d 143*0 16080471 47*0 46080471 15*0 c6080471 15*0 1a0800c1 175*0 10*180000c2
  //   32 d 20*0 82 10*14000472 40005
  //   contents of rom_2 (hex, n*v repeats v):
  //   768*0 5fa0000e 6fa0000e 7fa0000e 8fa0000e 9fa0000e afa0000e bfa0000e cfa0000e dfa0000e efa0000e
  //   e8000004 21*0 7400011 efa00001 dfa00001 cfa00001 bfa00001 afa00001 9fa00001 8fa00001 7fa00001
  //   6fa00001 5fa00000
  //   Program counter
  //   Program memory
  //   contents of rom_3 (hex, n*v repeats v):
  //   2fffc0f 300000f 1ffff05 1ffff06 1ffff07 1ffff08 1ffff09 1ffff0a 1ffff0b 1ffff0c 1ffff0d 1000300
  //   1000501 3000000d 0 1ffff05 1ffff06 1ffff07 1ffff08 1ffff09 1ffff0a 1ffff0b 1ffff0c 1ffff0d 5000100
  //   32000000 1000005 1000006 1000007 1000008 1000009 100000a 100000b 100000c 100000d 30ffffec 32000000
endmodule

module regfile (
  input  [31:0] in_1,
  input  in_2,
  input  in_3,
  input  in_4,
  input  in_5,
  input  [3:0] in_6,
  input  in_7,
  input  [3:0] in_8,
  input  in_9,
  input  [3:0] in_10,
  input  in_11,
  input  in_12,
  output [31:0] out_13,
  output [31:0] out_14,
  output [31:0] out_15,
  output [31:0] out_16,
  output [31:0] out_17,
  output [31:0] out_18,
  output [31:0] out_19,
  output [31:0] out_20,
  output [31:0] out_21,
  output [31:0] out_22,
  output [31:0] out_23,
  output [31:0] out_24,
  output [31:0] out_25,
  output [31:0] out_26,
  output [31:0] out_27,
  output [31:0] out_28,
  output [31:0] out_29,
  output [31:0] out_30
);

  wire and_1_out, and_2_out, and_3_out, and_4_out, and_5_out, and_6_out, and_7_out, and_8_out, and_9_out,
       and_10_out, and_11_out, and_12_out, and_13_out, and_14_out, and_15_out, and_16_out, and_17_out,
       and_18_out, and_19_out, and_20_out, and_21_out, and_22_out, and_23_out, and_24_out, and_25_out,
       and_26_out, and_27_out, and_28_out, and_29_out, and_30_out, and_31_out, and_32_out, and_33_out,
       and_34_out, and_35_out, counter_1_carry, decoder_1_out0, decoder_1_out1, decoder_1_out2,
       decoder_1_out3, decoder_1_out4, decoder_1_out5, decoder_1_out6, decoder_1_out7, decoder_1_out8,
       decoder_1_out9, decoder_1_out10, decoder_1_out11, decoder_1_out12, decoder_1_out13, decoder_1_out14,
       decoder_1_out15, decoder_2_out0, decoder_2_out1, decoder_2_out2, decoder_2_out3, decoder_2_out4,
       decoder_2_out5, decoder_2_out6, decoder_2_out7, decoder_2_out8, decoder_2_out9, decoder_2_out10,
       decoder_2_out11, decoder_2_out12, decoder_2_out13, decoder_2_out14, decoder_2_out15, decoder_3_out0,
       decoder_3_out1, decoder_3_out2, decoder_3_out3, decoder_3_out4, decoder_3_out5, decoder_3_out6,
       decoder_3_out7, decoder_3_out8, decoder_3_out9, decoder_3_out10, decoder_3_out11, decoder_3_out12,
       decoder_3_out13, decoder_3_out14, decoder_3_out15, or_1_out, or_2_out, or_3_out, or_4_out, or_5_out;

  or or_1 (or_1_out, in_4, in_5);
  Pull_Resistor pull_resistor_1 (.node(out_29));
  Pull_Resistor pull_resistor_2 (.node(out_30));
  Decoder #(.select(4), .disabled(0)) decoder_1 (
    .out0(decoder_1_out0), .out1(decoder_1_out1), .out2(decoder_1_out2), .out3(decoder_1_out3),
    .out4(decoder_1_out4), .out5(decoder_1_out5), .out6(decoder_1_out6), .out7(decoder_1_out7),
    .out8(decoder_1_out8), .out9(decoder_1_out9), .out10(decoder_1_out10), .out11(decoder_1_out11),
    .out12(decoder_1_out12), .out13(decoder_1_out13), .out14(decoder_1_out14), .out15(decoder_1_out15),
    .sel(in_6), .en(or_1_out));
  Decoder #(.select(4), .disabled(0)) decoder_2 (
    .out0(decoder_2_out0), .out1(decoder_2_out1), .out2(decoder_2_out2), .out3(decoder_2_out3),
    .out4(decoder_2_out4), .out5(decoder_2_out5), .out6(decoder_2_out6), .out7(decoder_2_out7),
    .out8(decoder_2_out8), .out9(decoder_2_out9), .out10(decoder_2_out10), .out11(decoder_2_out11),
    .out12(decoder_2_out12), .out13(decoder_2_out13), .out14(decoder_2_out14), .out15(decoder_2_out15),
    .sel(in_8), .en(in_7));
  Decoder #(.select(4), .disabled(0)) decoder_3 (
    .out0(decoder_3_out0), .out1(decoder_3_out1), .out2(decoder_3_out2), .out3(decoder_3_out3),
    .out4(decoder_3_out4), .out5(decoder_3_out5), .out6(decoder_3_out6), .out7(decoder_3_out7),
    .out8(decoder_3_out8), .out9(decoder_3_out9), .out10(decoder_3_out10), .out11(decoder_3_out11),
    .out12(decoder_3_out12), .out13(decoder_3_out13), .out14(decoder_3_out14), .out15(decoder_3_out15),
    .sel(in_10), .en(in_9));
  and and_1 (and_1_out, decoder_1_out0, in_5);
  and and_2 (and_2_out, in_4, decoder_1_out0);
  Register #(.width(16)) register_1 (.D(in_1[15:0]), .en(and_1_out), .Q(out_15[15:0]), .clk(in_11), .clr(in_12));
  Register #(.width(16)) register_2 (.D(in_1[31:16]), .en(and_2_out), .Q(out_15[31:16]), .clk(in_11), .clr(in_12));
  assign out_29 = decoder_2_out0 ? out_15 : 32'bz;  // Controlled_Buffer controlled_buffer_1
  assign out_30 = decoder_3_out0 ? out_15 : 32'bz;  // Controlled_Buffer controlled_buffer_2
  and and_3 (and_3_out, decoder_1_out1, in_5);
  and and_4 (and_4_out, in_4, decoder_1_out1);
  Register #(.width(16)) register_3 (.D(in_1[15:0]), .en(and_3_out), .Q(out_16[15:0]), .clk(in_11), .clr(in_12));
  Register #(.width(16)) register_4 (.D(in_1[31:16]), .en(and_4_out), .Q(out_16[31:16]), .clk(in_11), .clr(in_12));
  assign out_29 = decoder_2_out1 ? out_16 : 32'bz;  // Controlled_Buffer controlled_buffer_3
  assign out_30 = decoder_3_out1 ? out_16 : 32'bz;  // Controlled_Buffer controlled_buffer_4
  and and_5 (and_5_out, decoder_1_out2, in_5);
  and and_6 (and_6_out, in_4, decoder_1_out2);
  Register #(.width(16)) register_5 (.D(in_1[15:0]), .en(and_5_out), .Q(out_17[15:0]), .clk(in_11), .clr(in_12));
  Register #(.width(16)) register_6 (.D(in_1[31:16]), .en(and_6_out), .Q(out_17[31:16]), .clk(in_11), .clr(in_12));
  assign out_29 = decoder_2_out2 ? out_17 : 32'bz;  // Controlled_Buffer controlled_buffer_5
  assign out_30 = decoder_3_out2 ? out_17 : 32'bz;  // Controlled_Buffer controlled_buffer_6
  Register #(.width(16)) register_7 (.D(in_1[15:0]), .en(and_7_out), .Q(out_18[15:0]), .clk(in_11), .clr(in_12));
  and and_7 (and_7_out, decoder_1_out3, in_5);
  Register #(.width(16)) register_8 (.D(in_1[31:16]), .en(and_8_out), .Q(out_18[31:16]), .clk(in_11), .clr(in_12));
  and and_8 (and_8_out, in_4, decoder_1_out3);
  assign out_30 = decoder_3_out3 ? out_18 : 32'bz;  // Controlled_Buffer controlled_buffer_7
  assign out_29 = decoder_2_out3 ? out_18 : 32'bz;  // Controlled_Buffer controlled_buffer_8
  Register #(.width(16)) register_9 (.D(in_1[15:0]), .en(and_9_out), .Q(out_19[15:0]), .clk(in_11), .clr(in_12));
  and and_9 (and_9_out, decoder_1_out4, in_5);
  Register #(.width(16)) register_10 (.D(in_1[31:16]), .en(and_10_out), .Q(out_19[31:16]), .clk(in_11), .clr(in_12));
  and and_10 (and_10_out, in_4, decoder_1_out4);
  assign out_30 = decoder_3_out4 ? out_19 : 32'bz;  // Controlled_Buffer controlled_buffer_9
  assign out_29 = decoder_2_out4 ? out_19 : 32'bz;  // Controlled_Buffer controlled_buffer_10
  and and_11 (and_11_out, decoder_1_out5, in_5);
  and and_12 (and_12_out, in_4, decoder_1_out5);
  Register #(.width(16)) register_11 (.D(in_1[15:0]), .en(and_11_out), .Q(out_20[15:0]), .clk(in_11), .clr(in_12));
  Register #(.width(16)) register_12 (.D(in_1[31:16]), .en(and_12_out), .Q(out_20[31:16]), .clk(in_11), .clr(in_12));
  assign out_29 = decoder_2_out5 ? out_20 : 32'bz;  // Controlled_Buffer controlled_buffer_11
  assign out_30 = decoder_3_out5 ? out_20 : 32'bz;  // Controlled_Buffer controlled_buffer_12
  and and_13 (and_13_out, decoder_1_out6, in_5);
  and and_14 (and_14_out, in_4, decoder_1_out6);
  Register #(.width(16)) register_13 (.D(in_1[15:0]), .en(and_13_out), .Q(out_21[15:0]), .clk(in_11), .clr(in_12));
  Register #(.width(16)) register_14 (.D(in_1[31:16]), .en(and_14_out), .Q(out_21[31:16]), .clk(in_11), .clr(in_12));
  assign out_30 = decoder_3_out6 ? out_21 : 32'bz;  // Controlled_Buffer controlled_buffer_13
  assign out_29 = decoder_2_out6 ? out_21 : 32'bz;  // Controlled_Buffer controlled_buffer_14
  and and_15 (and_15_out, decoder_1_out7, in_5);
  and and_16 (and_16_out, in_4, decoder_1_out7);
  Register #(.width(16)) register_15 (.D(in_1[15:0]), .en(and_15_out), .Q(out_22[15:0]), .clk(in_11), .clr(in_12));
  Register #(.width(16)) register_16 (.D(in_1[31:16]), .en(and_16_out), .Q(out_22[31:16]), .clk(in_11), .clr(in_12));
  assign out_29 = decoder_2_out7 ? out_22 : 32'bz;  // Controlled_Buffer controlled_buffer_15
  assign out_30 = decoder_3_out7 ? out_22 : 32'bz;  // Controlled_Buffer controlled_buffer_16
  and and_17 (and_17_out, decoder_1_out8, in_5);
  and and_18 (and_18_out, in_4, decoder_1_out8);
  Register #(.width(16)) register_17 (.D(in_1[15:0]), .en(and_17_out), .Q(out_23[15:0]), .clk(in_11), .clr(in_12));
  Register #(.width(16)) register_18 (.D(in_1[31:16]), .en(and_18_out), .Q(out_23[31:16]), .clk(in_11), .clr(in_12));
  assign out_29 = decoder_2_out8 ? out_23 : 32'bz;  // Controlled_Buffer controlled_buffer_17
  assign out_30 = decoder_3_out8 ? out_23 : 32'bz;  // Controlled_Buffer controlled_buffer_18
  and and_19 (and_19_out, decoder_1_out9, in_5);
  and and_20 (and_20_out, in_4, decoder_1_out9);
  Register #(.width(16)) register_19 (.D(in_1[15:0]), .en(and_19_out), .Q(out_24[15:0]), .clk(in_11), .clr(in_12));
  Register #(.width(16)) register_20 (.D(in_1[31:16]), .en(and_20_out), .Q(out_24[31:16]), .clk(in_11), .clr(in_12));
  assign out_29 = decoder_2_out9 ? out_24 : 32'bz;  // Controlled_Buffer controlled_buffer_19
  assign out_30 = decoder_3_out9 ? out_24 : 32'bz;  // Controlled_Buffer controlled_buffer_20
  and and_21 (and_21_out, decoder_1_out10, in_5);
  and and_22 (and_22_out, in_4, decoder_1_out10);
  Register #(.width(16)) register_21 (.D(in_1[15:0]), .en(and_21_out), .Q(out_25[15:0]), .clk(in_11), .clr(in_12));
  Register #(.width(16)) register_22 (.D(in_1[31:16]), .en(and_22_out), .Q(out_25[31:16]), .clk(in_11), .clr(in_12));
  assign out_29 = decoder_2_out10 ? out_25 : 32'bz;  // Controlled_Buffer controlled_buffer_21
  assign out_30 = decoder_3_out10 ? out_25 : 32'bz;  // Controlled_Buffer controlled_buffer_22
  Register #(.width(16)) register_23 (.D(in_1[15:0]), .en(and_23_out), .Q(out_26[15:0]), .clk(in_11), .clr(in_12));
  and and_23 (and_23_out, decoder_1_out11, in_5);
  Register #(.width(16)) register_24 (.D(in_1[31:16]), .en(and_24_out), .Q(out_26[31:16]), .clk(in_11), .clr(in_12));
  and and_24 (and_24_out, in_4, decoder_1_out11);
  assign out_29 = decoder_2_out11 ? out_26 : 32'bz;  // Controlled_Buffer controlled_buffer_23
  assign out_30 = decoder_3_out11 ? out_26 : 32'bz;  // Controlled_Buffer controlled_buffer_24
  Register #(.width(16)) register_25 (.D(in_1[15:0]), .en(and_25_out), .Q(out_27[15:0]), .clk(in_11), .clr(in_12));
  and and_25 (and_25_out, decoder_1_out12, in_5);
  Register #(.width(16)) register_26 (.D(in_1[31:16]), .en(and_26_out), .Q(out_27[31:16]), .clk(in_11), .clr(in_12));
  and and_26 (and_26_out, in_4, decoder_1_out12);
  assign out_29 = decoder_2_out12 ? out_27 : 32'bz;  // Controlled_Buffer controlled_buffer_25
  assign out_30 = decoder_3_out12 ? out_27 : 32'bz;  // Controlled_Buffer controlled_buffer_26
  and and_27 (and_27_out, decoder_1_out13, in_5);
  and and_28 (and_28_out, in_4, decoder_1_out13);
  Register #(.width(16)) register_27 (.D(in_1[15:0]), .en(and_27_out), .Q(out_28[15:0]), .clk(in_11), .clr(in_12));
  Register #(.width(16)) register_28 (.D(in_1[31:16]), .en(and_28_out), .Q(out_28[31:16]), .clk(in_11), .clr(in_12));
  assign out_29 = decoder_2_out13 ? out_28 : 32'bz;  // Controlled_Buffer controlled_buffer_27
  assign out_30 = decoder_3_out13 ? out_28 : 32'bz;  // Controlled_Buffer controlled_buffer_28
  and and_29 (and_29_out, decoder_1_out14, in_5);
  and and_30 (and_30_out, in_4, decoder_1_out14);
  Register #(.width(16)) register_29 (.D(in_1[15:0]), .en(and_29_out), .Q(out_13[15:0]), .clk(in_11), .clr(in_12));
  Register #(.width(16)) register_30 (.D(in_1[31:16]), .en(and_30_out), .Q(out_13[31:16]), .clk(in_11), .clr(in_12));
  assign out_29 = decoder_2_out14 ? out_13 : 32'bz;  // Controlled_Buffer controlled_buffer_29
  assign out_30 = decoder_3_out14 ? out_13 : 32'bz;  // Controlled_Buffer controlled_buffer_30
  and and_31 (and_31_out, decoder_1_out15, in_5);
  and and_32 (and_32_out, in_4, decoder_1_out15);
  or or_2 (or_2_out, in_2, and_31_out);
  or or_3 (or_3_out, and_31_out, and_32_out);
  or or_4 (or_4_out, and_32_out, and_33_out);
  and and_33 (and_33_out, counter_1_carry, in_2);
  and and_34 (and_34_out, or_5_out, ~or_3_out);  // AND_Gate
  and and_35 (and_35_out, ~or_3_out, counter_1_carry, or_5_out);  // AND_Gate
  or or_5 (or_5_out, in_2, in_3);
  Register #(.width(2)) register_31 (.D(in_1[1:0]), .en(and_31_out), .Q(out_14[1:0]), .clk(in_11), .clr(in_12));
  Counter #(.width(14), .max('h3fff)) counter_1 (
    .load(or_2_out), .D(in_1[15:2]), .count(and_34_out), .Q(out_14[15:2]), .carry(counter_1_carry),
    .clk(in_11), .clr(in_12));
  Counter #(.width(16), .max('hffff)) counter_2 (
    .load(or_4_out), .D(in_1[31:16]), .count(and_35_out), .Q(out_14[31:16]), .clk(in_11), .clr(in_12));  // open: carry
  assign out_29 = decoder_2_out15 ? out_14 : 32'bz;  // Controlled_Buffer controlled_buffer_31
  assign out_30 = decoder_3_out15 ? out_14 : 32'bz;  // Controlled_Buffer controlled_buffer_32
endmodule

module ALU (
);

  wire adder_1_cout, undriven_3, undriven_4, undriven_5, undriven_6, undriven_8;
  wire [1:0] undriven_7;
  wire [4:0] bit_extender_1_out;
  wire [31:0] adder_1_out, and_1_out, multiplexer_1_out, multiplexer_2_out, multiplexer_3_out,
       multiplexer_4_out, multiplexer_5_out, not_1_out, not_2_out, not_3_out, shifter_1_out, shifter_2_out,
       undriven, undriven_2, xor_1_out;

  Multiplexer #(.width(32), .disabled(0), .enable("false")) multiplexer_1 (
    .in0(undriven), .in1(not_1_out), .out(multiplexer_1_out), .sel(undriven_3));
  assign not_1_out = ~undriven;  // NOT_Gate not_1, 32 bits wide
  assign not_2_out = ~undriven_2;  // NOT_Gate not_2, 32 bits wide
  Multiplexer #(.width(32), .disabled(0), .enable("false")) multiplexer_2 (
    .in0(undriven_2), .in1(not_2_out), .out(multiplexer_2_out), .sel(undriven_4));
  Adder #(.width(32)) adder_1 (
    .a(multiplexer_1_out), .b(multiplexer_2_out), .out(adder_1_out), .cin(undriven_5), .cout(adder_1_cout));
  assign and_1_out = multiplexer_2_out & multiplexer_1_out;  // AND_Gate and_1, 32 bits wide
  assign xor_1_out = multiplexer_1_out ^ multiplexer_2_out;  // XOR_Gate xor_1, 32 bits wide
  Bit_Extender #(.in_width(32), .out_width(5)) bit_extender_1 (.in(multiplexer_2_out), .out(bit_extender_1_out));
  Shifter #(.width(32)) shifter_1 (.in(multiplexer_1_out), .\dist (bit_extender_1_out), .out(shifter_1_out));
  Shifter #(.width(32), .shift("lr")) shifter_2 (
    .in(multiplexer_1_out), .\dist (bit_extender_1_out), .out(shifter_2_out));
  Multiplexer #(.width(32), .disabled(0), .enable("false")) multiplexer_3 (
    .in0(shifter_1_out), .in1(shifter_2_out), .out(multiplexer_3_out), .sel(undriven_6));
  Multiplexer #(.select(2), .width(32), .disabled(0), .enable("false")) multiplexer_4 (
    .in0(adder_1_out), .in1(and_1_out), .in2(xor_1_out), .in3(multiplexer_3_out), .out(multiplexer_4_out),
    .sel(undriven_7));
  assign not_3_out = ~multiplexer_4_out;  // NOT_Gate not_3, 32 bits wide
  Multiplexer #(.width(32), .disabled(0), .enable("false")) multiplexer_5 (
    .in0(multiplexer_4_out), .in1(not_3_out), .out(multiplexer_5_out), .sel(undriven_8));
endmodule
